// Logisim project CA-B2-alu_design_and_implementation-v00.circ as structural Verilog: 3 circuits, main circuit Full_Adder_1bit
module Full_Adder_1bit (
  input  A,
  input  B,
  input  Cin,
  output Sum,
  output Cout
);

  wire and_1_out, and_2_out, xor_1_out;

  xor xor_1 (xor_1_out, A, B);
  and and_1 (and_1_out, xor_1_out, Cin);
  and and_2 (and_2_out, A, B);
  xor xor_2 (Sum, xor_1_out, Cin);
  or or_1 (Cout, and_1_out, and_2_out);
endmodule

module AdderSubtractor_1bit (
  input  A,
  input  B,
  input  Op,
  input  Cin,
  output Sum,
  output Cout
);

  wire xor_1_out;

  xor xor_1 (xor_1_out, B, Op);
  Full_Adder_1bit full_adder_1bit_1 (.A(A), .B(xor_1_out), .Cin(Cin), .Sum(Sum), .Cout(Cout));
endmodule

module AdderSubtractor_16bit (
  input  Op,
  input  [15:0] B,
  input  [15:0] A,
  output [15:0] out_4,
  output out_5
);

  wire addersubtractor_1bit_1_cout, addersubtractor_1bit_2_cout, addersubtractor_1bit_3_cout,
       addersubtractor_1bit_4_cout, addersubtractor_1bit_5_cout, addersubtractor_1bit_6_cout,
       addersubtractor_1bit_7_cout, addersubtractor_1bit_8_cout, addersubtractor_1bit_9_cout,
       addersubtractor_1bit_10_cout, addersubtractor_1bit_11_cout, addersubtractor_1bit_12_cout,
       addersubtractor_1bit_13_cout, addersubtractor_1bit_14_cout, addersubtractor_1bit_15_cout;

  // Probe on A
  AdderSubtractor_1bit addersubtractor_1bit_1 (
    .A(A[0]), .B(B[0]), .Op(Op), .Cin(Op), .Sum(out_4[0]), .Cout(addersubtractor_1bit_1_cout));
  AdderSubtractor_1bit addersubtractor_1bit_2 (
    .A(A[1]), .B(B[1]), .Op(Op), .Cin(addersubtractor_1bit_1_cout), .Sum(out_4[1]),
    .Cout(addersubtractor_1bit_2_cout));
  AdderSubtractor_1bit addersubtractor_1bit_3 (
    .A(A[2]), .B(B[2]), .Op(Op), .Cin(addersubtractor_1bit_2_cout), .Sum(out_4[2]),
    .Cout(addersubtractor_1bit_3_cout));
  AdderSubtractor_1bit addersubtractor_1bit_4 (
    .A(A[3]), .B(B[3]), .Op(Op), .Cin(addersubtractor_1bit_3_cout), .Sum(out_4[3]),
    .Cout(addersubtractor_1bit_4_cout));
  AdderSubtractor_1bit addersubtractor_1bit_5 (
    .A(A[4]), .B(B[4]), .Op(Op), .Cin(addersubtractor_1bit_4_cout), .Sum(out_4[4]),
    .Cout(addersubtractor_1bit_5_cout));
  AdderSubtractor_1bit addersubtractor_1bit_6 (
    .A(A[5]), .B(B[5]), .Op(Op), .Cin(addersubtractor_1bit_5_cout), .Sum(out_4[5]),
    .Cout(addersubtractor_1bit_6_cout));
  AdderSubtractor_1bit addersubtractor_1bit_7 (
    .A(A[6]), .B(B[6]), .Op(Op), .Cin(addersubtractor_1bit_6_cout), .Sum(out_4[6]),
    .Cout(addersubtractor_1bit_7_cout));
  AdderSubtractor_1bit addersubtractor_1bit_8 (
    .A(A[7]), .B(B[7]), .Op(Op), .Cin(addersubtractor_1bit_7_cout), .Sum(out_4[7]),
    .Cout(addersubtractor_1bit_8_cout));
  AdderSubtractor_1bit addersubtractor_1bit_9 (
    .A(A[8]), .B(B[8]), .Op(Op), .Cin(addersubtractor_1bit_8_cout), .Sum(out_4[8]),
    .Cout(addersubtractor_1bit_9_cout));
  AdderSubtractor_1bit addersubtractor_1bit_10 (
    .A(A[9]), .B(B[9]), .Op(Op), .Cin(addersubtractor_1bit_9_cout), .Sum(out_4[9]),
    .Cout(addersubtractor_1bit_10_cout));
  AdderSubtractor_1bit addersubtractor_1bit_11 (
    .A(A[10]), .B(B[10]), .Op(Op), .Cin(addersubtractor_1bit_10_cout), .Sum(out_4[10]),
    .Cout(addersubtractor_1bit_11_cout));
  AdderSubtractor_1bit addersubtractor_1bit_12 (
    .A(A[11]), .B(B[11]), .Op(Op), .Cin(addersubtractor_1bit_11_cout), .Sum(out_4[11]),
    .Cout(addersubtractor_1bit_12_cout));
  AdderSubtractor_1bit addersubtractor_1bit_13 (
    .A(A[12]), .B(B[12]), .Op(Op), .Cin(addersubtractor_1bit_12_cout), .Sum(out_4[12]),
    .Cout(addersubtractor_1bit_13_cout));
  AdderSubtractor_1bit addersubtractor_1bit_14 (
    .A(A[13]), .B(B[13]), .Op(Op), .Cin(addersubtractor_1bit_13_cout), .Sum(out_4[13]),
    .Cout(addersubtractor_1bit_14_cout));
  AdderSubtractor_1bit addersubtractor_1bit_15 (
    .A(A[14]), .B(B[14]), .Op(Op), .Cin(addersubtractor_1bit_14_cout), .Sum(out_4[14]),
    .Cout(addersubtractor_1bit_15_cout));
  AdderSubtractor_1bit addersubtractor_1bit_16 (
    .A(A[15]), .B(B[15]), .Op(Op), .Cin(addersubtractor_1bit_15_cout), .Sum(out_4[15]), .Cout(out_5));
  // Probe on out_4
  // Probe on B
endmodule
