// Logisim project Proyecto_ALU_IEEE.circ as structural Verilog: 15 circuits, main circuit Full_Adder_1bit
module Full_Adder_1bit (
  input  A,
  input  B,
  input  Cin,
  output Sum,
  output Cout
);

  wire and_1_out, and_2_out, xor_1_out;

  xor xor_1 (xor_1_out, A, B);
  and and_1 (and_1_out, xor_1_out, Cin);
  and and_2 (and_2_out, A, B);
  xor xor_2 (Sum, xor_1_out, Cin);
  or or_1 (Cout, and_1_out, and_2_out);
endmodule

module AdderSubtractor_1bit (
  input  A,
  input  B,
  input  Op,
  input  Cin,
  output Sum,
  output Cout
);

  wire xor_1_out;

  xor xor_1 (xor_1_out, B, Op);
  Full_Adder_1bit full_adder_1bit_1 (.A(A), .B(xor_1_out), .Cin(Cin), .Sum(Sum), .Cout(Cout));
endmodule

module AdderSubtractor_16bit (
  input  Op,
  input  [15:0] B,
  input  [15:0] A,
  output [15:0] Resultado,
  output Cout,
  output CarryInMSB
);

  wire addersubtractor_1bit_1_cout, addersubtractor_1bit_2_cout, addersubtractor_1bit_3_cout,
       addersubtractor_1bit_4_cout, addersubtractor_1bit_5_cout, addersubtractor_1bit_6_cout,
       addersubtractor_1bit_7_cout, addersubtractor_1bit_8_cout, addersubtractor_1bit_9_cout,
       addersubtractor_1bit_10_cout, addersubtractor_1bit_11_cout, addersubtractor_1bit_12_cout,
       addersubtractor_1bit_13_cout, addersubtractor_1bit_14_cout;

  // Probe on A
  AdderSubtractor_1bit addersubtractor_1bit_1 (
    .A(A[0]), .B(B[0]), .Op(Op), .Cin(Op), .Sum(Resultado[0]), .Cout(addersubtractor_1bit_1_cout));
  AdderSubtractor_1bit addersubtractor_1bit_2 (
    .A(A[1]), .B(B[1]), .Op(Op), .Cin(addersubtractor_1bit_1_cout), .Sum(Resultado[1]),
    .Cout(addersubtractor_1bit_2_cout));
  AdderSubtractor_1bit addersubtractor_1bit_3 (
    .A(A[2]), .B(B[2]), .Op(Op), .Cin(addersubtractor_1bit_2_cout), .Sum(Resultado[2]),
    .Cout(addersubtractor_1bit_3_cout));
  AdderSubtractor_1bit addersubtractor_1bit_4 (
    .A(A[3]), .B(B[3]), .Op(Op), .Cin(addersubtractor_1bit_3_cout), .Sum(Resultado[3]),
    .Cout(addersubtractor_1bit_4_cout));
  AdderSubtractor_1bit addersubtractor_1bit_5 (
    .A(A[4]), .B(B[4]), .Op(Op), .Cin(addersubtractor_1bit_4_cout), .Sum(Resultado[4]),
    .Cout(addersubtractor_1bit_5_cout));
  AdderSubtractor_1bit addersubtractor_1bit_6 (
    .A(A[5]), .B(B[5]), .Op(Op), .Cin(addersubtractor_1bit_5_cout), .Sum(Resultado[5]),
    .Cout(addersubtractor_1bit_6_cout));
  AdderSubtractor_1bit addersubtractor_1bit_7 (
    .A(A[6]), .B(B[6]), .Op(Op), .Cin(addersubtractor_1bit_6_cout), .Sum(Resultado[6]),
    .Cout(addersubtractor_1bit_7_cout));
  AdderSubtractor_1bit addersubtractor_1bit_8 (
    .A(A[7]), .B(B[7]), .Op(Op), .Cin(addersubtractor_1bit_7_cout), .Sum(Resultado[7]),
    .Cout(addersubtractor_1bit_8_cout));
  AdderSubtractor_1bit addersubtractor_1bit_9 (
    .A(A[8]), .B(B[8]), .Op(Op), .Cin(addersubtractor_1bit_8_cout), .Sum(Resultado[8]),
    .Cout(addersubtractor_1bit_9_cout));
  AdderSubtractor_1bit addersubtractor_1bit_10 (
    .A(A[9]), .B(B[9]), .Op(Op), .Cin(addersubtractor_1bit_9_cout), .Sum(Resultado[9]),
    .Cout(addersubtractor_1bit_10_cout));
  AdderSubtractor_1bit addersubtractor_1bit_11 (
    .A(A[10]), .B(B[10]), .Op(Op), .Cin(addersubtractor_1bit_10_cout), .Sum(Resultado[10]),
    .Cout(addersubtractor_1bit_11_cout));
  AdderSubtractor_1bit addersubtractor_1bit_12 (
    .A(A[11]), .B(B[11]), .Op(Op), .Cin(addersubtractor_1bit_11_cout), .Sum(Resultado[11]),
    .Cout(addersubtractor_1bit_12_cout));
  AdderSubtractor_1bit addersubtractor_1bit_13 (
    .A(A[12]), .B(B[12]), .Op(Op), .Cin(addersubtractor_1bit_12_cout), .Sum(Resultado[12]),
    .Cout(addersubtractor_1bit_13_cout));
  AdderSubtractor_1bit addersubtractor_1bit_14 (
    .A(A[13]), .B(B[13]), .Op(Op), .Cin(addersubtractor_1bit_13_cout), .Sum(Resultado[13]),
    .Cout(addersubtractor_1bit_14_cout));
  AdderSubtractor_1bit addersubtractor_1bit_15 (
    .A(A[14]), .B(B[14]), .Op(Op), .Cin(addersubtractor_1bit_14_cout), .Sum(Resultado[14]), .Cout(CarryInMSB));
  AdderSubtractor_1bit addersubtractor_1bit_16 (
    .A(A[15]), .B(B[15]), .Op(Op), .Cin(CarryInMSB), .Sum(Resultado[15]), .Cout(Cout));
  // Probe on Resultado
  // Probe on B
endmodule

// SHIFT
module Unidad_Desplazamiento_16bit (
  input  [15:0] A,
  input  Sel_Shift,
  output [15:0] Out_Shift
);

  Multiplexer #(.width(16), .enable("false")) multiplexer_1 (
    .in0({A[14:0], 1'b0}), .in1({1'b0, A[15:1]}), .out(Out_Shift), .sel(Sel_Shift));
endmodule

module Unidad_Logica_16bit (
  input  [15:0] A,
  input  [1:0] Sel_Logico,
  input  [15:0] B,
  output [15:0] Out_Logico
);

  wire [15:0] and_1_out, not_1_out, or_1_out, xor_1_out;

  assign and_1_out = A & B;  // AND_Gate and_1, 16 bits wide
  assign or_1_out = A | B;  // OR_Gate or_1, 16 bits wide
  assign xor_1_out = A ^ B;  // XOR_Gate xor_1, 16 bits wide
  assign not_1_out = ~A;  // NOT_Gate not_1, 16 bits wide
  Multiplexer #(.select(2), .width(16), .enable("false")) multiplexer_1 (
    .in0(and_1_out), .in1(or_1_out), .in2(xor_1_out), .in3(not_1_out), .out(Out_Logico), .sel(Sel_Logico));
endmodule

module Flags (
  input  [15:0] Resultado,
  input  CarryOut,
  input  CarryInMSB,
  output Zero,
  output Sign,
  output Carry,
  output Overflow
);

  xor xor_1 (Overflow, CarryOut, CarryInMSB);
  Comparator #(.width(16)) comparator_1 (.a({16{1'b0}}), .b(Resultado), .eq(Zero));  // open: gt, lt

  assign Carry = CarryOut;
  assign Sign = Resultado[15];
endmodule

module ALU_16bit_Principal (
  input  Sel_Arit,
  input  [15:0] A,
  input  [15:0] B,
  input  [1:0] Sel_Unidad,
  input  [1:0] Sel_Logico,
  input  Sel_Shift,
  output Zero,
  output Sign,
  output [15:0] Resultado,
  output Carry,
  output Overflow
);

  wire AddSub_carryinmsb, AddSub_cout, multiplexer_2_out, multiplexer_3_out;
  wire [15:0] AddSub_resultado, Logic_out_logico, Shift_out_shift;

  // Probe on A
  // Probe on B
  AdderSubtractor_16bit AddSub (
    .Op(Sel_Arit), .A(A), .CarryInMSB(AddSub_carryinmsb), .Cout(AddSub_cout), .B(B),
    .Resultado(AddSub_resultado));
  Unidad_Logica_16bit Logic (.A(A), .Sel_Logico(Sel_Logico), .B(B), .Out_Logico(Logic_out_logico));
  Unidad_Desplazamiento_16bit Shift (.Out_Shift(Shift_out_shift), .A(A), .Sel_Shift(Sel_Shift));
  Multiplexer #(.select(2), .width(16), .enable("false")) multiplexer_1 (
    .in0(AddSub_resultado), .in1(Logic_out_logico), .in2(Shift_out_shift), .in3({16{1'b0}}), .out(Resultado),
    .sel(Sel_Unidad));
  // Probe on Resultado
  Multiplexer #(.select(2), .enable("false")) multiplexer_2 (
    .in0(AddSub_cout), .in1(1'b0), .in2(1'b0), .in3(1'b0), .out(multiplexer_2_out), .sel(Sel_Unidad));
  Multiplexer #(.select(2), .enable("false")) multiplexer_3 (
    .in0(AddSub_carryinmsb), .in1(1'b0), .in2(1'b0), .in3(1'b0), .out(multiplexer_3_out), .sel(Sel_Unidad));
  Flags Flags (
    .Resultado(Resultado), .CarryOut(multiplexer_2_out), .CarryInMSB(multiplexer_3_out), .Zero(Zero),
    .Sign(Sign), .Carry(Carry), .Overflow(Overflow));
endmodule

module IEEE754_Extractor (
  input  [15:0] IEEE_In,
  output [9:0] Mantisa,
  output [4:0] Exponent,
  output Sign
);


  assign Exponent = IEEE_In[14:10];
  assign Mantisa = IEEE_In[9:0];
  assign Sign = IEEE_In[15];
endmodule

module IEEE754_Comparator (
  input  [4:0] Exponente__A,
  input  [4:0] Exponente_B,
  output Mayor_Es_A,
  output ExpIguales,
  output [4:0] Exponente_Mayor,
  output [4:0] Diferencia
);

  wire [4:0] multiplexer_2_out;

  Comparator #(.width(5)) comparator_1 (
    .a(Exponente__A), .b(Exponente_B), .gt(Mayor_Es_A), .eq(ExpIguales));  // open: lt
  Multiplexer #(.width(5), .enable("false")) multiplexer_1 (
    .in0(Exponente_B), .in1(Exponente__A), .out(Exponente_Mayor), .sel(Mayor_Es_A));
  Multiplexer #(.width(5), .enable("false")) multiplexer_2 (
    .in0(Exponente__A), .in1(Exponente_B), .out(multiplexer_2_out), .sel(Mayor_Es_A));
  Subtractor #(.width(5)) subtractor_1 (
    .a(Exponente_Mayor), .b(multiplexer_2_out), .out(Diferencia));  // open: bin, bout
endmodule

module IEEE_Alligner (
  input  [4:0] Exponente_Mayor,
  input  Mayor_Es_A,
  input  ExpIguales,
  input  [9:0] Mantisa_A,
  input  [9:0] Mantisa_B,
  input  [4:0] Diferencia,
  output [4:0] ExpOut,
  output MayorFinal,
  output [10:0] MantMayor,
  output [10:0] MantMenor
);

  wire comparator_1_eq, comparator_1_gt, or_1_out;
  wire [10:0] multiplexer_2_out;

  Comparator #(.width(11)) comparator_1 (
    .a({1'b1, Mantisa_A}), .b({1'b1, Mantisa_B}), .gt(comparator_1_gt), .eq(comparator_1_eq));  // open: lt
  Multiplexer #(.width(11), .enable("false")) multiplexer_1 (
    .in0({1'b1, Mantisa_B}), .in1({1'b1, Mantisa_A}), .out(MantMayor), .sel(MayorFinal));
  Multiplexer #(.width(11), .enable("false")) multiplexer_2 (
    .in0({1'b1, Mantisa_A}), .in1({1'b1, Mantisa_B}), .out(multiplexer_2_out), .sel(MayorFinal));
  or or_1 (or_1_out, comparator_1_gt, comparator_1_eq);
  Multiplexer #(.enable("false")) multiplexer_3 (.in0(Mayor_Es_A), .in1(or_1_out), .out(MayorFinal), .sel(ExpIguales));
  Shifter #(.width(11), .shift("lr")) shifter_1 (.in(multiplexer_2_out), .\dist (Diferencia[3:0]), .out(MantMenor));

  assign ExpOut = Exponente_Mayor;
endmodule

module IEEE754_MantissaALU (
  input  [4:0] ExpOut,
  input  MayorFinal,
  input  SignA,
  input  SignB,
  input  [10:0] MantMayor,
  input  [10:0] MantMenor,
  output [4:0] ExpTemp,
  output SignOut,
  output [11:0] MantTemp
);

  wire multiplexer_2_out, xor_1_out;
  wire [10:0] adder_1_out, subtractor_1_out;
  wire [11:11] adder_1_cout;

  Adder #(.width(11)) adder_1 (.a(MantMayor), .b(MantMenor), .out(adder_1_out), .cout(adder_1_cout[11]));  // open: cin
  Subtractor #(.width(11)) subtractor_1 (.a(MantMayor), .b(MantMenor), .out(subtractor_1_out));  // open: bin, bout
  xor xor_1 (xor_1_out, SignA, SignB);
  Multiplexer #(.enable("false")) multiplexer_1 (.in0(SignA), .in1(multiplexer_2_out), .out(SignOut), .sel(xor_1_out));
  Multiplexer #(.enable("false")) multiplexer_2 (.in0(SignB), .in1(SignA), .out(multiplexer_2_out), .sel(MayorFinal));
  Multiplexer #(.width(12), .enable("false")) multiplexer_3 (
    .in0({adder_1_cout[11], adder_1_out}), .in1({1'b0, subtractor_1_out}), .out(MantTemp), .sel(xor_1_out));

  assign ExpTemp = ExpOut;
endmodule

module IEEE754_Normalizer (
  input  SignOut,
  input  [11:0] MantTemp,
  input  [4:0] ExpTemp,
  output SignNorm,
  output [4:0] ExpNorm,
  output [10:0] MantNorm
);

  wire and_1_out, and_2_out, and_3_out, and_4_out, comparator_1_eq, not_1_out, not_2_out, not_3_out,
       not_4_out, not_5_out, not_6_out, not_7_out;
  wire [2:0] or_1_out;
  wire [4:0] adder_1_out, multiplexer_3_out, subtractor_1_out;
  wire [11:0] multiplexer_1_out, shifter_1_out, shifter_2_out;
  wire [11:11] multiplexer_2_out;

  Comparator #(.width(12)) comparator_1 (.a(MantTemp), .b({12{1'b0}}), .eq(comparator_1_eq));  // open: gt, lt
  not not_1 (not_1_out, MantTemp[11]);
  not not_2 (not_2_out, MantTemp[10]);
  not not_3 (not_3_out, comparator_1_eq);
  and and_1 (and_1_out, MantTemp[9], not_4_out);
  not not_4 (not_4_out, MantTemp[10]);
  Shifter #(.width(12)) shifter_1 (.in(MantTemp), .\dist ({1'b0, or_1_out}), .out(shifter_1_out));
  Shifter #(.width(12), .shift("lr")) shifter_2 (.in(MantTemp), .\dist (4'b0001), .out(shifter_2_out));
  and and_2 (and_2_out, not_1_out, not_2_out, not_3_out);
  and and_3 (and_3_out, MantTemp[8], not_4_out, not_5_out);
  not not_5 (not_5_out, MantTemp[9]);
  Multiplexer #(.width(12), .enable("false")) multiplexer_1 (
    .in0(MantTemp), .in1(shifter_2_out), .out(multiplexer_1_out), .sel(MantTemp[11]));
  and and_4 (and_4_out, MantTemp[7], not_4_out, not_5_out, not_6_out);
  not not_6 (not_6_out, MantTemp[8]);
  Multiplexer #(.width(12), .enable("false")) multiplexer_2 (
    .in0(multiplexer_1_out), .in1(shifter_1_out), .out({multiplexer_2_out[11], MantNorm}), .sel(and_2_out));
  and and_5 (or_1_out[2], MantTemp[6], not_4_out, not_5_out, not_6_out, not_7_out);
  not not_7 (not_7_out, MantTemp[7]);
  or or_1 (or_1_out[0], and_4_out, and_1_out);
  Subtractor #(.width(5)) subtractor_1 (.a(ExpTemp), .b({2'b00, or_1_out}), .out(subtractor_1_out));  // open: bin, bout
  Adder #(.width(5)) adder_1 (.a(ExpTemp), .b(5'b00001), .out(adder_1_out));  // open: cin, cout
  or or_2 (or_1_out[1], and_4_out, and_3_out);
  Multiplexer #(.width(5), .enable("false")) multiplexer_3 (
    .in0(ExpTemp), .in1(adder_1_out), .out(multiplexer_3_out), .sel(MantTemp[11]));
  Multiplexer #(.width(5), .enable("false")) multiplexer_4 (
    .in0(multiplexer_3_out), .in1(subtractor_1_out), .out(ExpNorm), .sel(and_2_out));

  assign SignNorm = SignOut;

  // Other names for the same wires on the sheet: CarryMant = MantTemp[11]
endmodule

module IEEE754_Packer (
  input  [10:0] MantNorm,
  input  [4:0] ExpNorm,
  input  SignNorm,
  output [15:0] IEEE754_Out
);


  assign IEEE754_Out = {SignNorm, ExpNorm, MantNorm[9:0]};
endmodule

module IEEE754_Principal (
  input  [15:0] A,
  input  [15:0] B,
  output [15:0] IEEE_Result
);

  wire Alligner_mayorfinal, Comparator_expiguales, Comparator_mayor_es_a, Extractor_A_sign, Extractor_B_sign,
       MantissaALU_signout, Normalizer_signnorm;
  wire [4:0] Alligner_expout, Comparator_diferencia, Comparator_exponente_mayor, Extractor_A_exponent,
       Extractor_B_exponent, MantissaALU_exptemp, Normalizer_expnorm;
  wire [9:0] Extractor_A_mantisa, Extractor_B_mantisa;
  wire [10:0] Alligner_mantmayor, Alligner_mantmenor, Normalizer_mantnorm;
  wire [11:0] MantissaALU_manttemp;

  IEEE754_Extractor Extractor_A (
    .IEEE_In(A), .Mantisa(Extractor_A_mantisa), .Exponent(Extractor_A_exponent), .Sign(Extractor_A_sign));
  IEEE754_Extractor Extractor_B (
    .IEEE_In(B), .Mantisa(Extractor_B_mantisa), .Exponent(Extractor_B_exponent), .Sign(Extractor_B_sign));
  IEEE754_Comparator Comparator (
    .Exponente__A(Extractor_A_exponent), .Exponente_B(Extractor_B_exponent),
    .Mayor_Es_A(Comparator_mayor_es_a), .ExpIguales(Comparator_expiguales),
    .Exponente_Mayor(Comparator_exponente_mayor), .Diferencia(Comparator_diferencia));
  IEEE_Alligner Alligner (
    .Exponente_Mayor(Comparator_exponente_mayor), .Mayor_Es_A(Comparator_mayor_es_a),
    .Mantisa_A(Extractor_A_mantisa), .Mantisa_B(Extractor_B_mantisa), .Diferencia(Comparator_diferencia),
    .ExpIguales(Comparator_expiguales), .ExpOut(Alligner_expout), .MayorFinal(Alligner_mayorfinal),
    .MantMayor(Alligner_mantmayor), .MantMenor(Alligner_mantmenor));
  IEEE754_MantissaALU MantissaALU (
    .ExpOut(Alligner_expout), .SignA(Extractor_A_sign), .SignB(Extractor_B_sign),
    .MantMayor(Alligner_mantmayor), .MantMenor(Alligner_mantmenor), .MayorFinal(Alligner_mayorfinal),
    .ExpTemp(MantissaALU_exptemp), .SignOut(MantissaALU_signout), .MantTemp(MantissaALU_manttemp));
  IEEE754_Normalizer Normalizer (
    .SignOut(MantissaALU_signout), .MantTemp(MantissaALU_manttemp), .ExpTemp(MantissaALU_exptemp),
    .SignNorm(Normalizer_signnorm), .ExpNorm(Normalizer_expnorm), .MantNorm(Normalizer_mantnorm));
  IEEE754_Packer Packer (
    .MantNorm(Normalizer_mantnorm), .ExpNorm(Normalizer_expnorm), .SignNorm(Normalizer_signnorm),
    .IEEE754_Out(IEEE_Result));
endmodule

module Circuito_Principal (
  input  [15:0] A,
  input  [15:0] B,
  input  SelArit,
  input  [1:0] SelLogic,
  input  SelShift,
  input  [1:0] SelUnidad,
  input  ModeIEEE,
  output [15:0] Resultado,
  output Zero,
  output Carry,
  output Overflow,
  output Sign
);

  wire ALU16bits_carry, ALU16bits_overflow, ALU16bits_sign, ALU16bits_zero;
  wire [15:0] ALU16bits_resultado, IEEE754_ieee_result;

  Multiplexer #(.enable("false")) multiplexer_1 (.in0(ALU16bits_overflow), .in1(1'b0), .out(Overflow), .sel(ModeIEEE));
  Multiplexer #(.enable("false")) multiplexer_2 (.in0(ALU16bits_carry), .in1(1'b0), .out(Carry), .sel(ModeIEEE));
  Multiplexer #(.enable("false")) multiplexer_3 (.in0(ALU16bits_sign), .in1(1'b0), .out(Sign), .sel(ModeIEEE));
  Multiplexer #(.enable("false")) multiplexer_4 (.in0(ALU16bits_zero), .in1(1'b0), .out(Zero), .sel(ModeIEEE));
  IEEE754_Principal IEEE754 (.A(A), .B(B), .IEEE_Result(IEEE754_ieee_result));
  ALU_16bit_Principal ALU16bits (
    .Sel_Arit(SelArit), .A(A), .Zero(ALU16bits_zero), .B(B), .Sign(ALU16bits_sign), .Carry(ALU16bits_carry),
    .Overflow(ALU16bits_overflow), .Sel_Logico(SelLogic), .Sel_Shift(SelShift), .Sel_Unidad(SelUnidad),
    .Resultado(ALU16bits_resultado));
  Multiplexer #(.width(16), .enable("false")) multiplexer_5 (
    .in0(ALU16bits_resultado), .in1(IEEE754_ieee_result), .out(Resultado), .sel(ModeIEEE));
endmodule
